# Fritzing sketch ardubeer_fritz (saved by Fritzing 0.9.3b)
breadboards: 2

parts:
  Part1 = Arduino Uno (Rev3)
  LED1 = LED - 5mm [color="Blue (505nm)" package="5 mm [THT]"]
  LED2 = LED - 5mm [color="Green (555nm)" package="5 mm [THT]"]
  LED3 = LED - 5mm [color="Orange (620nm)" package="5 mm [THT]"]
  S1 = Round Pushbutton
  YF-S201_Flow_Meter1 = YF-S201 Water Flow Meter
  R1 = Resistor [tolerance=±5% resistance=10k package="1206 [SMD]"]
  R2 = Resistor [tolerance=±5% resistance=10k package="1206 [SMD]"]
  LED4 = LED - 5mm [color="Red (660nm)" package="5 mm [THT]"]
  LED5 = LED - 5mm [color="Blue (525nm)" package="5 mm [THT]"]
  LED6 = LED - 5mm [color="Orange (605nm)" package="5 mm [THT]"]
  R3 = Resistor [tolerance=±5% resistance=220 package="1206 [SMD]"]
  R4 = Resistor [tolerance=±5% resistance=220 package="1206 [SMD]"]
  R5 = Resistor [tolerance=±5% resistance=220 package="1206 [SMD]"]

nets:
  N1: Part1.D9_PWM, LED3.anode
  N2: Part1.D10_PWM/SS, LED6.anode
  N3: Part1.D11_PWM/MOSI, LED5.anode
  N4: Part1.D12/MISO, LED4.anode
  N5: Part1.D3_PWM, YF-S201_Flow_Meter1.SIG, R1.Pin_0
  N6: Part1.D5_PWM, LED1.anode
  N7: Part1.D6_PWM, LED2.anode
  N8: Part1.D7, S1.leg0, R2.Pin_1
  5V: Part1.5V, S1.leg1, YF-S201_Flow_Meter1.VCC, R1.Pin_1
  GND: Part1.GND, LED1.cathode, LED2.cathode, LED3.cathode, YF-S201_Flow_Meter1.GND, R2.Pin_0, R3.Pin_1, R4.Pin_1, R5.Pin_1
  N9: LED4.cathode, R3.Pin_0
  N10: LED5.cathode, R4.Pin_0
  N11: LED6.cathode, R5.Pin_0

notes:
  PUSH TO FILL BOTTLE
  FLOW METER
  beerfillPin
  co2Pin
  liftSolenoidPin
  ORANGE LED = POWER
  GREEN LED = READY
  BLUE LED = BUSY FILLING
  220Ω
  10kΩ

custom parts:
  YF-S201 Water Flow Meter: The YF-S201 Flow Meter. The input voltage is 5V to 24V (DC).

// code stored in the sketch: ardubeerCode.ino
/*


ARDUBEER v0.2  


Client: 


Glenn Adams 
EMAIL: glenn.adams@mweb.co.za


STAINLESS MARINE
www.microbrewingsa.co.za
083 709 6759
22 Fish Eagle Park
Kommetjie


- - - - - - - - - - - - - - - - - - - - - - - - - - - - - - - - - - - - - - - - - -


Coded by Rouan van der Ende
EMAIL: bitlabio@gmail.com
PHONE: 062 933 1183


------------------------------------------------------------------------------------*/


int pulsecount = 0;


int startButtonPin = 7;


int beerfillPin     = 10;
int co2Pin          = 11;
int liftSolenoidPin = 12;
int flowPulsePin    = 3; //Arduino UNO interrupt only on pin 2 or 3.


//LEDS (PWM so we can wire up directly without resistors)
int powerLED = 9;
int readyLED = 5;
int flowLED = 6;


bool filling        = 0; //0 = not filling, 1 = filling.


/*------------------------------------------------------------------------------------*/


void setup() {


  //LEDS
  pinMode(powerLED, OUTPUT);
  pinMode(readyLED, OUTPUT);
  pinMode(flowLED, OUTPUT);


  analogWrite(powerLED, 100); //0-255 brightness
  analogWrite(readyLED, 100);
  analogWrite(flowLED, 0);



  pinMode(beerfillPin,OUTPUT);      
  pinMode(liftSolenoidPin,OUTPUT);  
  pinMode(co2Pin,OUTPUT);            


  // beer flow sensor:
  pinMode(flowPulsePin, INPUT_PULLUP); 
  
  // this should run the flowpulse() function each time a pulse is detected.
  attachInterrupt(digitalPinToInterrupt(flowPulsePin), flowpulse, CHANGE); 
}


/*------------------------------------------------------------------------------------*/


void loop() {
  if (filling == false) {
    int buttonstate = digitalRead(startButtonPin);
    if (buttonstate == 1) {
      startfill();
    }
  }
}


/*------------------------------------------------------------------------------------*/


void startfill() {
    // This function is called when the button is pushed to start the bottle fill process.


    digitalWrite(liftSolenoidPin, HIGH);  // open valve
    digitalWrite(co2Pin, HIGH);           // open CO2


    delay(5000);                          // wait 5 sec


    digitalWrite(co2Pin, LOW);            // close CO2
    digitalWrite(liftSolenoidPin, LOW);   // close valve


    // start beer fill


    digitalWrite(beerfillPin, HIGH);
    filling = true;
}


/*------------------------------------------------------------------------------------*/


void flowpulse() {
  // This function is called each time the flow pulse is sensed.
  if (filling == true) {
    pulsecount++;
    analogWrite(flowLED, 25+((pulsecount%2)*75)); //should toggle between two brightness when filling on each pulse.
    if (pulsecount >= 12760 ) {
      // beer should be full now.
      pulsecount = 0; // zero counter
      
      endfill();      // bottle full.
    }
  }
}


/*------------------------------------------------------------------------------------*/


void endfill() {
  // Stop beer flow:
  filling = false;
  analogWrite(flowLED, 0);              // turn off flow light
  digitalWrite(beerfillPin, LOW);       // turn off beer pin


  // After filling up do this:  
  delay(6000);                          // wait a bit
  digitalWrite(liftSolenoidPin, LOW);   // close pneumatics.
  // delay(3000);                       // if needed uncomment.
}
